// Logisim project final_risc2_ (1).circ as structural Verilog: 4 circuits, main circuit main
module main (
);

  wire ALURAM, ALUZERO, CLK, RESET;
  wire [1:0] ALUOP, PCMODE;
  wire [2:0] multiplexer_1_out;
  wire [5:0] ALU_output, multiplexer_2_out, multiplexer_3_out, ram_1_data, REG_File_r1out, REG_RT;
  wire [7:0] PLAOUT;
  wire [11:0] ABS, PC_out;
  wire [15:12] INSTRUCTION;

  Clock clock_1 (.out(CLK));
  // Probe on PC_out
  PC PC (.CLK(CLK), .ABS(ABS), .PCMODE(PCMODE), .IMM(ABS[5:0]), .RESET(RESET), .OUT(PC_out));
  ROM #(.addrWidth(12), .dataWidth(16)) rom_1 (.addr(PC_out), .data({INSTRUCTION, ABS}));  // open: sel
  // Probe on INSTRUCTION
  // Probe on ABS[2:0]
  // PLA pla_1: pin names not known; wires that end beside it: INSTRUCTION, {ABS[2], 1'b0, ALUZERO, 1'b0, ABS[1:0], INSTRUCTION}, {ABS[2], 1'b0, ALUZERO, 1'b0, ABS[1:0], INSTRUCTION}, {PCMODE, ALUOP, PLAOUT[7:4], ALURAM, PLAOUT[2:0]}
  // Probe on {PCMODE, ALUOP, PLAOUT[7:4], ALURAM, PLAOUT[2:0]}
  Multiplexer #(.width(3)) multiplexer_1 (
    .in0(ABS[5:3]), .in1(ABS[8:6]), .out(multiplexer_1_out), .sel(PLAOUT[6]));  // open: en
  REG_File REG_File (
    .CLK(CLK), .IN(multiplexer_3_out), .WEN(PLAOUT[7]), .WIN(multiplexer_1_out), .R1IN(ABS[11:9]),
    .R2IN(ABS[8:6]), .R1OUT(REG_File_r1out), .R2OUT(REG_RT));
  Multiplexer #(.width(6)) multiplexer_2 (
    .in0(REG_RT), .in1(ABS[5:0]), .out(multiplexer_2_out), .sel(PLAOUT[5]));  // open: en
  ALU ALU (.A(REG_File_r1out), .zero(ALUZERO), .B(multiplexer_2_out), .Operation(ALUOP), .Output(ALU_output));
  RAM #(.addrWidth(6), .dataWidth(6), .bus("separate")) ram_1 (
    .addr(ALU_output), .din(REG_RT), .data(ram_1_data), .str(PLAOUT[4]), .clk(CLK));  // open: sel, ld, clr
  Multiplexer #(.width(6)) multiplexer_3 (
    .in0(ALU_output), .in1(ram_1_data), .out(multiplexer_3_out), .sel(ALURAM));  // open: en

  // Other names for the same wires on the sheet: OPCODE[3:0] = INSTRUCTION; FUNC[2:0] = ABS[2:0]; IMM[5:0] = ABS[5:0];
  //   INSTRUCTION[11:0] = ABS; RD[2:0] = ABS[5:3]; RT[2:0] = ABS[8:6]; RS[2:0] = ABS[11:9];
  //   PLAOUT (some bits) = {PCMODE, ALUOP, ALURAM}; WRAM = PLAOUT[4]; RTIMM = PLAOUT[5]; RDRT = PLAOUT[6];
  //   WEN = PLAOUT[7]

  // Notes on the sheet:
  //   contents of rom_1 (hex, n*v repeats v):
  //   e000 e0c1 c00a e1d0 c012 f440 c4d3 c5f1 1c3c 4241 c4d0 f440 143d c2cb 33a0 2c01 d004 d011
endmodule

module PC (
  input  CLK,
  input  [11:0] ABS,
  input  [1:0] PCMODE,
  input  [5:0] IMM,
  input  RESET,
  output [11:0] OUT
);

  wire [11:0] adder_1_out, adder_2_out, bit_extender_1_out, multiplexer_1_out;

  Multiplexer #(.select(2), .width(12)) multiplexer_1 (
    .in0(adder_1_out), .in1(adder_2_out), .in2(ABS), .out(multiplexer_1_out), .sel(PCMODE));  // open: in3, en
  Register #(.width(12), .trigger("falling")) PR (.D(multiplexer_1_out), .Q(OUT), .clk(CLK), .clr(RESET));  // open: en
  Adder #(.width(12)) adder_1 (.a(OUT), .b(12'h1), .out(adder_1_out));  // open: cin, cout
  assign bit_extender_1_out = {{6{IMM[5]}}, IMM};  // Bit_Extender bit_extender_1
  Adder #(.width(12)) adder_2 (.a(adder_1_out), .b(bit_extender_1_out), .out(adder_2_out));  // open: cin, cout
endmodule

module REG_File (
  input  CLK,
  input  [5:0] IN,
  input  WEN,
  input  [2:0] WIN,
  input  [2:0] R1IN,
  input  [2:0] R2IN,
  output [5:0] R1OUT,
  output [5:0] R2OUT
);

  wire and_1_out, and_2_out, and_3_out, and_4_out, and_5_out, and_6_out, and_7_out, and_8_out,
       decoder_1_out0, decoder_1_out1, decoder_1_out2, decoder_1_out3, decoder_1_out4, decoder_1_out5,
       decoder_1_out6, decoder_1_out7;
  wire [5:0] R0_q, R1_q, R2_q, R3_q, R4_q, R5_q, R6_q, R7_q;

  Decoder #(.select(3)) decoder_1 (
    .out0(decoder_1_out0), .out1(decoder_1_out1), .out2(decoder_1_out2), .out3(decoder_1_out3),
    .out4(decoder_1_out4), .out5(decoder_1_out5), .out6(decoder_1_out6), .out7(decoder_1_out7), .sel(WIN));  // open: en
  and and_1 (and_1_out, WEN, decoder_1_out0);
  and and_2 (and_2_out, WEN, decoder_1_out1);
  and and_3 (and_3_out, WEN, decoder_1_out2);
  and and_4 (and_4_out, WEN, decoder_1_out3);
  and and_5 (and_5_out, WEN, decoder_1_out4);
  and and_6 (and_6_out, WEN, decoder_1_out5);
  and and_7 (and_7_out, WEN, decoder_1_out6);
  and and_8 (and_8_out, WEN, decoder_1_out7);
  Register #(.width(6), .trigger("falling")) R0 (.D(IN), .en(and_1_out), .Q(R0_q), .clk(CLK));  // open: clr
  Register #(.width(6), .trigger("falling")) R1 (.D(IN), .en(and_2_out), .Q(R1_q), .clk(CLK));  // open: clr
  Register #(.width(6), .trigger("falling")) R2 (.D(IN), .en(and_3_out), .Q(R2_q), .clk(CLK));  // open: clr
  Register #(.width(6), .trigger("falling")) R3 (.D(IN), .en(and_4_out), .Q(R3_q), .clk(CLK));  // open: clr
  Register #(.width(6), .trigger("falling")) R4 (.D(IN), .en(and_5_out), .Q(R4_q), .clk(CLK));  // open: clr
  Register #(.width(6), .trigger("falling")) R5 (.D(IN), .en(and_6_out), .Q(R5_q), .clk(CLK));  // open: clr
  Register #(.width(6), .trigger("falling")) R6 (.D(IN), .en(and_7_out), .Q(R6_q), .clk(CLK));  // open: clr
  Register #(.width(6), .trigger("falling")) R7 (.D(IN), .en(and_8_out), .Q(R7_q), .clk(CLK));  // open: clr
  Multiplexer #(.select(3), .width(6)) multiplexer_1 (
    .in0(R0_q), .in1(R1_q), .in2(R2_q), .in3(R3_q), .in4(R4_q), .in5(R5_q), .in6(R6_q), .in7(R7_q),
    .out(R2OUT), .sel(R2IN));  // open: en
  Multiplexer #(.select(3), .width(6)) multiplexer_2 (
    .in0(R0_q), .in1(R1_q), .in2(R2_q), .in3(R3_q), .in4(R4_q), .in5(R5_q), .in6(R6_q), .in7(R7_q),
    .out(R1OUT), .sel(R1IN));  // open: en
endmodule

module ALU (
  input  [5:0] A,
  input  [5:0] B,
  input  [1:0] Operation,
  output [5:0] Output,
  output zero
);

  wire subtractor_1_bout;
  wire [5:0] adder_1_out, bit_extender_1_out, subtractor_1_out;

  Adder #(.width(6)) adder_1 (.a(A), .b(B), .out(adder_1_out));  // open: cin, cout
  Subtractor #(.width(6)) subtractor_1 (.a(A), .b(B), .out(subtractor_1_out), .bout(subtractor_1_bout));  // open: bin
  assign bit_extender_1_out = {{5{1'b0}}, subtractor_1_bout};  // Bit_Extender bit_extender_1
  Multiplexer #(.select(2), .width(6), .enable("false")) multiplexer_1 (
    .in0(adder_1_out), .in1(subtractor_1_out), .in2(bit_extender_1_out), .in3(B), .out(Output),
    .sel(Operation));
  Comparator #(.width(6)) comparator_1 (.a(Output), .b({6{1'b0}}), .eq(zero));  // open: gt, lt
endmodule
